# Fritzing sketch schematics-slider (saved by Fritzing 1.0.4)
breadboards: 1

parts:
  S1 = Pushbutton [package="[THT]"]
  R1 = Rotary Potentiometer (Small) [maximum_resistance=10kΩ knob_status=50% power=0.5W package=THT]
  S3 = Pushbutton [package="[THT]"]
  Composant1 = Arduino Uno (Rev3)
  HC-SR04_Sensor_1 = HC-SR04 Ultrasonic Distance Sensor
  HC-SR04_Sensor_2 = HC-SR04 Ultrasonic Distance Sensor

nets:
  N1: S1.Pin_3, S1.Pin_4, Composant1.A0
  GND: R1.leg1, S3.Pin_1, S3.Pin_2, Composant1.GND, HC-SR04_Sensor_1.GND, HC-SR04_Sensor_2.GND
  VCC: R1.leg2, Composant1.5V, HC-SR04_Sensor_1.VCC, HC-SR04_Sensor_2.VCC
  N2: S3.Pin_3, S3.Pin_4, Composant1.D2
  N3: Composant1.D3_PWM, HC-SR04_Sensor_2.ECHO
  N4: Composant1.D4, HC-SR04_Sensor_2.TRIG
  N5: Composant1.D5_PWM, HC-SR04_Sensor_1.TRIG
  N6: Composant1.D6_PWM, HC-SR04_Sensor_1.ECHO
